# Fritzing sketch my first fritzing (saved by Fritzing 0.9.3b)
breadboards: 1

parts:
  Part1 = Arduino Uno (Rev3)
  LED1 = LED - 5mm [color="Red (633nm)" package="5 mm [THT]"]
  R1 = Resistor [tolerance=±5% resistance=220 package=THT]
  LED2 = LED - 5mm [color="Blue (430nm)" package="5 mm [THT]"]
  R2 = Resistor [tolerance=±5% resistance=220 package=THT]
  S1 = Pushbutton [package="[THT]"]
  S2 = Pushbutton [package="[THT]"]
  R3 = Resistor [tolerance=±5% resistance=10k package=THT]
  R4 = Resistor [tolerance=±5% resistance=10k package=THT]

nets:
  N1: Part1.D12/MISO, LED2.cathode
  N2: Part1.D13/SCK, LED1.cathode
  N3: Part1.D2, S2.Pin_3, S2.Pin_4, R4.Pin_0
  N4: Part1.D7, S1.Pin_3, S1.Pin_4
  N5: Part1.5V, S2.Pin_1, S2.Pin_2
  N6: Part1.GND, R1.Pin_1, R2.Pin_1, R3.Pin_1, R4.Pin_1
  N7: LED1.anode, R1.Pin_0
  N8: LED2.anode, R2.Pin_0
  N9: S1.Pin_1, S1.Pin_2, R3.Pin_0

// code stored in the sketch: Untitled2.ino
int led=13;

void setup() {
  // put your setup code here, to run once:
Serial.begin (9600);
pinMode (13, OUTPUT); 
pinMode (12, OUTPUT);

}

void loop() {
  // put your main code here, to run repeatedly:
digitalWrite(13, HIGH);
delay (350);
digitalWrite(13, LOW);
delay (350);

digitalWrite(12, HIGH);
delay(350);
digitalWrite(12, LOW);
delay(350);


}
