# Fritzing sketch useless box fritz (saved by Fritzing 0.9.3b)
breadboards: 1

parts:
  Part1 = Arduino Uno (Rev3)  # not connected
  VCC1 = Battery block 9V
  R2 = Resistor [tolerance=±5% resistance=220 package=THT]
  Part2 = Prototyping Shield
  J1 = Basic Servo
  S6 = Toggle Switch [package=THT]
  S7 = Toggle Switch [package=THT]
  LED1 = LED - 5mm [color="Red (633nm)" package="5 mm [THT]"]
  R3 = Resistor [tolerance=±5% resistance=220 package=THT]

nets:
  N1: VCC1.-, Part2.GND#99
  N2: VCC1.+, Part2.VIN
  N3: R2.Pin_0, Part2.D4, S6.L2
  N4: R2.Pin_1, Part2.GND#98
  N5: Part2.D8, J1.pulse
  N6: Part2.D10_PWM/SS, Part2.5V#94, LED1.cathode
  N7: Part2.5V#87, J1.vcc
  N8: Part2.GND#88, Part2.GND#89, J1.gnd, S7.L2
  N9: Part2.5V#96, S6.COM
  N10: Part2.GND#101, R3.Pin_0
  N11: S7.COM, LED1.anode

custom parts:
  Prototyping Shield: The Arduino Uno is a microcontroller board based on the ATmega328 (datasheet). It has 14 digital input/output pins (of which 6 can be used as PWM outputs), 6 analog inputs, a 16 MHz ceramic resonator, a USB connection, a power jack, an ICSP header, and a reset button. It contains everything needed to support the microcontroller; simply connect it to a computer with a USB cable or power it with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
